// Digital circuit Lab02.dig as structural Verilog
module Lab02 (
  input  B,
  input  C,
  input  A,
  input  D,
  output Fa,
  output Fb,
  output Fc,
  output Fd,
  output Fe,
  output Fg,
  output Ff
);

  wire A_t, AB, AC, and_5_out, and_6_out, and_7_out, and_8_out, and_9_out, and_10_out, and_11_out,
       and_12_out, and_13_out, and_14_out, and_15_out, and_16_out, and_17_out, and_18_out, and_19_out,
       and_20_out, and_21_out, and_22_out, and_23_out, and_24_out, and_25_out, and_26_out, and_27_out, B_D,
       B_t, C_t, CD, D_t;

  and and_1 (B_D, B_t, D_t);
  and and_2 (AC, A, C);
  and and_3 (AB, A, B_t);
  and and_4 (CD, C, D_t);
  Seven_Seg seven_seg_1 (.a(Fa), .b(Fb), .c(Fc), .d(Fd), .e(Fe), .f(Ff), .g(Fg), .dp(1'b0));
  not not_1 (A_t, A);
  not not_2 (B_t, B);
  not not_3 (C_t, C);
  not not_4 (D_t, D);
  and and_5 (and_5_out, A_t, C);
  and and_6 (and_6_out, A_t, B, D);
  and and_7 (and_7_out, B, C);
  and and_8 (and_8_out, A, B_t, C_t);
  and and_9 (and_9_out, A_t, B_t);
  and and_10 (and_10_out, A, C_t, D);
  and and_11 (and_11_out, A_t, C, D);
  and and_12 (and_12_out, A_t, C_t, D_t);
  and and_13 (and_13_out, A_t, B);
  and and_14 (and_14_out, A_t, D);
  and and_15 (and_15_out, C_t, D);
  and and_16 (and_16_out, A_t, C_t);
  and and_17 (and_17_out, A, C_t);
  and and_18 (and_18_out, B, C, D_t);
  and and_19 (and_19_out, B, C_t, D);
  and and_20 (and_20_out, B_t, C, D);
  and and_21 (and_21_out, A_t, B_t, D_t);
  and and_22 (and_22_out, A, B);
  and and_23 (and_23_out, A_t, B, C_t);
  and and_24 (and_24_out, A_t, B, D_t);
  and and_25 (and_25_out, A_t, C_t, D_t);
  and and_26 (and_26_out, B, C_t);
  and and_27 (and_27_out, B_t, C);
  or or_1 (Fa, B_D, and_5_out, and_6_out, and_7_out, and_8_out);
  or or_2 (Fb, B_D, and_9_out, and_10_out, and_11_out, and_12_out);
  or or_3 (Fc, AB, and_13_out, and_14_out, and_15_out, and_16_out);
  or or_4 (Fd, and_17_out, and_18_out, and_19_out, and_20_out, and_21_out);
  or or_5 (Fe, and_22_out, AC, CD, B_D);
  or or_6 (Ff, AC, and_23_out, and_24_out, and_25_out, AB);
  or or_7 (Fg, and_26_out, A, CD, and_27_out);
endmodule
